// Logisim project 2bit_full_adder.circ as structural Verilog: 1 circuit, main circuit main
module main (
  input  B1,
  input  B0,
  input  A1,
  input  A0,
  output S2,
  output S1,
  output S0
);

  wire main_2_out_3, nand_1_out, nand_2_out, nand_3_out, nand_4_out;

  XOR_NAND_main main_1 (.in_1(A0), .in_2(B0), .out_3(S0));
  nand nand_1 (nand_1_out, A0, B0);
  XOR_NAND_main main_2 (.in_1(A1), .in_2(B1), .out_3(main_2_out_3));
  nand nand_2 (nand_2_out, A1, B1);
  nand nand_3 (nand_3_out, nand_1_out, nand_1_out);
  XOR_NAND_main main_3 (.in_1(main_2_out_3), .in_2(nand_3_out), .out_3(S1));
  nand nand_4 (nand_4_out, nand_3_out, main_2_out_3);
  nand nand_5 (S2, nand_4_out, nand_2_out);
endmodule
