// Logisim project 3bit_full_adder.circ as structural Verilog: 1 circuit, main circuit main
module main (
  input  B2,
  input  B1,
  input  B0,
  input  A2,
  input  A1,
  input  A0,
  output S0,
  output S1,
  output S2,
  output S3
);

  wire main_2_out_3, main_3_out_3, nand_1_out, nand_2_out, nand_3_out, nand_4_out, nand_5_out, nand_6_out,
       nand_7_out;

  XOR_NAND_main main_1 (.in_1(A0), .in_2(B0), .out_3(S0));
  nand nand_1 (nand_1_out, A0, B0);
  XOR_NAND_main main_2 (.in_1(A1), .in_2(B1), .out_3(main_2_out_3));
  nand nand_2 (nand_2_out, A1, B1);
  XOR_NAND_main main_3 (.in_1(A2), .in_2(B2), .out_3(main_3_out_3));
  nand nand_3 (nand_3_out, A2, B2);
  nand nand_4 (nand_4_out, nand_1_out, nand_1_out);
  XOR_NAND_main main_4 (.in_1(main_2_out_3), .in_2(nand_4_out), .out_3(S1));
  nand nand_5 (nand_5_out, nand_4_out, main_2_out_3);
  XOR_NAND_main main_5 (.in_1(main_3_out_3), .in_2(nand_7_out), .out_3(S2));
  nand nand_6 (nand_6_out, nand_7_out, main_3_out_3);
  nand nand_7 (nand_7_out, nand_5_out, nand_2_out);
  nand nand_8 (S3, nand_6_out, nand_3_out);
endmodule
