// Logisim project 4bit_register.circ as structural Verilog: 1 circuit, main circuit main
module main (
  input  Load,
  input  in_2,
  input  in_3,
  input  in_4,
  input  in_5,
  output out_6,
  output out_7,
  output out_8,
  output out_9
);

  wire and_1_out, and_2_out, and_3_out, and_4_out, clk_out;

  Clock clk (.out(clk_out));
  D_flipflop_main main_1 (.D(and_1_out), .Clock(clk_out), .Q(out_6));  // open: Q_prime
  and and_1 (and_1_out, Load, in_2);
  D_flipflop_main main_2 (.D(and_2_out), .Clock(clk_out), .Q(out_9));  // open: Q_prime
  D_flipflop_main main_3 (.D(and_3_out), .Clock(clk_out), .Q(out_8));  // open: Q_prime
  D_flipflop_main main_4 (.D(and_4_out), .Clock(clk_out), .Q(out_7));  // open: Q_prime
  and and_2 (and_2_out, Load, in_5);
  and and_3 (and_3_out, Load, in_4);
  and and_4 (and_4_out, Load, in_3);
endmodule
