// Logisim project AxorBxorCxorD using NOR.circ as structural Verilog: 1 circuit, main circuit main
module main (
  input  D,
  input  C,
  input  B,
  input  A,
  output out_5
);

  wire nor_1_out, nor_2_out, nor_3_out, nor_4_out, nor_5_out, nor_6_out, nor_7_out, nor_8_out, nor_9_out,
       nor_10_out, nor_11_out, nor_12_out, nor_13_out, nor_14_out;

  nor nor_1 (nor_1_out, A, A);
  nor nor_2 (nor_2_out, B, B);
  nor nor_3 (nor_3_out, nor_1_out, nor_2_out);
  nor nor_4 (nor_4_out, A, B);
  nor nor_5 (nor_5_out, nor_7_out, nor_7_out);
  nor nor_6 (nor_6_out, C, C);
  nor nor_7 (nor_7_out, nor_3_out, nor_4_out);
  nor nor_8 (nor_8_out, nor_5_out, nor_6_out);
  nor nor_9 (nor_9_out, nor_7_out, C);
  nor nor_10 (nor_10_out, nor_12_out, nor_12_out);
  nor nor_11 (nor_11_out, D, D);
  nor nor_12 (nor_12_out, nor_8_out, nor_9_out);
  nor nor_13 (nor_13_out, nor_10_out, nor_11_out);
  nor nor_14 (nor_14_out, nor_12_out, D);
  nor nor_15 (out_5, nor_13_out, nor_14_out);
endmodule
