// Logisim project BCD_to_Excess-3_MUX.circ as structural Verilog: 1 circuit, main circuit main
module main (
  input  _0,
  input  _1,
  input  A,
  input  [2:0] BCD,
  output W,
  output X,
  output Y,
  output Z
);

  wire not_1_out;

  not not_1 (not_1_out, A);
  Multiplexer #(.select(3), .disabled(0), .enable("false")) multiplexer_1 (
    .in0(A), .in1(A), .in2(_0), .in3(_0), .in4(_0), .in5(not_1_out), .in6(not_1_out), .in7(not_1_out),
    .out(W), .sel(BCD));
  Multiplexer #(.select(3), .disabled(0), .enable("false")) multiplexer_2 (
    .in0(_0), .in1(_1), .in2(not_1_out), .in3(not_1_out), .in4(not_1_out), .in5(_0), .in6(_0), .in7(_0),
    .out(X), .sel(BCD));
  Multiplexer #(.select(3), .disabled(0), .enable("false")) multiplexer_3 (
    .in0(_1), .in1(_0), .in2(_0), .in3(not_1_out), .in4(not_1_out), .in5(_0), .in6(_0), .in7(not_1_out),
    .out(Y), .sel(BCD));
  Multiplexer #(.select(3)) multiplexer_4 (
    .in0(_1), .in1(_0), .in2(not_1_out), .in3(_0), .in4(not_1_out), .in5(_0), .in6(not_1_out), .in7(_0),
    .out(Z), .sel(BCD));  // open: en
endmodule
