// Logisim project Binary to Decimal.circ as structural Verilog: 1 circuit, main circuit main
module main (
  input  B3,
  input  B2,
  input  B1,
  input  B0,
  output _9,
  output _8,
  output _7,
  output _6,
  output _5,
  output _4,
  output _3,
  output _2,
  output _1,
  output _0
);

  wire nand_1_out, nand_2_out, nand_3_out, nand_4_out, nand_5_out, nand_8_out, nand_9_out, nand_10_out,
       nand_11_out, nand_12_out, nand_13_out, nand_14_out, nand_15_out, nand_16_out, nand_17_out,
       nand_18_out, nand_19_out, nand_20_out, nand_21_out, nand_22_out, nand_23_out, nand_24_out,
       nand_25_out, nand_26_out, nand_27_out, nand_28_out, nand_29_out, nand_30_out, nand_31_out,
       nand_32_out, nand_39_out, nand_40_out, nand_41_out, nand_42_out;

  nand nand_1 (nand_1_out, B3, B3);
  nand nand_2 (nand_2_out, B1, B1);
  nand nand_3 (nand_3_out, B2, B2);
  nand nand_4 (nand_4_out, B0, B0);
  nand nand_5 (nand_5_out, B3, B0);
  nand nand_6 (_9, nand_5_out, nand_5_out);
  nand nand_7 (_8, nand_8_out, nand_8_out);
  nand nand_8 (nand_8_out, B3, nand_4_out);
  nand nand_9 (nand_9_out, B2, B1);
  nand nand_10 (nand_10_out, nand_9_out, nand_9_out);
  nand nand_11 (nand_11_out, B2, B1);
  nand nand_12 (nand_12_out, nand_11_out, nand_11_out);
  nand nand_13 (nand_13_out, B2, nand_2_out);
  nand nand_14 (nand_14_out, nand_13_out, nand_13_out);
  nand nand_15 (nand_15_out, nand_16_out, nand_16_out);
  nand nand_16 (nand_16_out, B2, nand_2_out);
  nand nand_17 (nand_17_out, nand_3_out, B1);
  nand nand_18 (nand_18_out, nand_17_out, nand_17_out);
  nand nand_19 (nand_19_out, nand_3_out, B1);
  nand nand_20 (nand_20_out, nand_19_out, nand_19_out);
  nand nand_21 (nand_21_out, nand_1_out, nand_3_out);
  nand nand_22 (nand_22_out, nand_21_out, nand_21_out);
  nand nand_23 (nand_23_out, nand_1_out, nand_3_out);
  nand nand_24 (nand_24_out, nand_23_out, nand_23_out);
  nand nand_25 (nand_25_out, nand_10_out, B0);
  nand nand_26 (nand_26_out, nand_12_out, nand_4_out);
  nand nand_27 (nand_27_out, nand_14_out, B0);
  nand nand_28 (nand_28_out, nand_15_out, nand_4_out);
  nand nand_29 (nand_29_out, nand_18_out, B0);
  nand nand_30 (nand_30_out, nand_20_out, nand_4_out);
  nand nand_31 (nand_31_out, nand_22_out, nand_2_out);
  nand nand_32 (nand_32_out, nand_24_out, nand_2_out);
  nand nand_33 (_7, nand_25_out, nand_25_out);
  nand nand_34 (_6, nand_26_out, nand_26_out);
  nand nand_35 (_5, nand_27_out, nand_27_out);
  nand nand_36 (_4, nand_28_out, nand_28_out);
  nand nand_37 (_3, nand_29_out, nand_29_out);
  nand nand_38 (_2, nand_30_out, nand_30_out);
  nand nand_39 (nand_39_out, nand_31_out, nand_31_out);
  nand nand_40 (nand_40_out, nand_32_out, nand_32_out);
  nand nand_41 (nand_41_out, nand_39_out, B0);
  nand nand_42 (nand_42_out, nand_40_out, nand_4_out);
  nand nand_43 (_1, nand_41_out, nand_41_out);
  nand nand_44 (_0, nand_42_out, nand_42_out);
endmodule
