// Logisim project Decimal to Binary.circ as structural Verilog: 1 circuit, main circuit main
module main (
  input  _9,
  input  _8,
  input  _7,
  input  _6,
  input  _5,
  input  _4,
  input  _3,
  input  _2,
  input  _1,
  input  _0,
  output B3,
  output B2,
  output B1,
  output B0
);

  wire nand_1_out, nand_2_out, nand_3_out, nand_4_out, nand_5_out, nand_6_out, nand_7_out, nand_8_out,
       nand_9_out, nand_10_out, nand_12_out, nand_13_out, nand_14_out, nand_15_out, nand_16_out, nand_17_out,
       nand_18_out, nand_19_out, nand_20_out, nand_21_out, nand_24_out, nand_25_out;

  nand nand_1 (nand_1_out, _9, _9);
  nand nand_2 (nand_2_out, _8, _8);
  nand nand_3 (nand_3_out, _5, _5);
  nand nand_4 (nand_4_out, _7, _7);
  nand nand_5 (nand_5_out, _6, _6);
  nand nand_6 (nand_6_out, _4, _4);
  nand nand_7 (nand_7_out, _3, _3);
  nand nand_8 (nand_8_out, _2, _2);
  nand nand_9 (nand_9_out, _1, _1);
  nand nand_10 (nand_10_out, _0, _0);
  nand nand_11 (B3, nand_2_out, nand_1_out);
  nand nand_12 (nand_12_out, nand_6_out, nand_3_out);
  nand nand_13 (nand_13_out, nand_5_out, nand_4_out);
  nand nand_14 (nand_14_out, nand_8_out, nand_7_out);
  nand nand_15 (nand_15_out, nand_9_out, nand_7_out);
  nand nand_16 (nand_16_out, nand_3_out, nand_4_out);
  nand nand_17 (nand_17_out, nand_12_out, nand_12_out);
  nand nand_18 (nand_18_out, nand_13_out, nand_13_out);
  nand nand_19 (nand_19_out, nand_14_out, nand_14_out);
  nand nand_20 (nand_20_out, nand_15_out, nand_15_out);
  nand nand_21 (nand_21_out, nand_16_out, nand_16_out);
  nand nand_22 (B2, nand_17_out, nand_18_out);
  nand nand_23 (B1, nand_18_out, nand_19_out);
  nand nand_24 (nand_24_out, nand_20_out, nand_21_out);
  nand nand_25 (nand_25_out, nand_24_out, nand_24_out);
  nand nand_26 (B0, nand_25_out, nand_1_out);
endmodule
