// Logisim project 4bit_full_adder.circ as structural Verilog: 1 circuit, main circuit main
module main (
  input  [3:0] B,
  input  [3:0] A,
  output [3:0] S0,
  output Carry
);

  wire main_2_out_3, main_3_out_3, main_4_out_3, nand_1_out, nand_2_out, nand_3_out, nand_4_out, nand_5_out,
       nand_6_out, nand_7_out, nand_8_out, nand_9_out, nand_10_out;

  XOR_NAND_main main_1 (.in_1(A[0]), .in_2(B[0]), .out_3(S0[0]));
  nand nand_1 (nand_1_out, A[0], B[0]);
  XOR_NAND_main main_2 (.in_1(A[1]), .in_2(B[1]), .out_3(main_2_out_3));
  nand nand_2 (nand_2_out, A[1], B[1]);
  XOR_NAND_main main_3 (.in_1(A[2]), .in_2(B[2]), .out_3(main_3_out_3));
  nand nand_3 (nand_3_out, A[2], B[2]);
  XOR_NAND_main main_4 (.in_1(A[3]), .in_2(B[3]), .out_3(main_4_out_3));
  nand nand_4 (nand_4_out, A[3], B[3]);
  nand nand_5 (nand_5_out, nand_1_out, nand_1_out);
  XOR_NAND_main main_5 (.in_1(main_2_out_3), .in_2(nand_5_out), .out_3(S0[1]));
  nand nand_6 (nand_6_out, nand_5_out, main_2_out_3);
  XOR_NAND_main main_6 (.in_1(main_3_out_3), .in_2(nand_9_out), .out_3(S0[2]));
  nand nand_7 (nand_7_out, nand_9_out, main_3_out_3);
  XOR_NAND_main main_7 (.in_1(main_4_out_3), .in_2(nand_10_out), .out_3(S0[3]));
  nand nand_8 (nand_8_out, nand_10_out, main_4_out_3);
  nand nand_9 (nand_9_out, nand_6_out, nand_2_out);
  nand nand_10 (nand_10_out, nand_7_out, nand_3_out);
  nand nand_11 (Carry, nand_8_out, nand_4_out);

  // Notes on the sheet:
  //   4 bit full adder
endmodule
