// Logisim project PIPOresistor4bit.circ as structural Verilog: 1 circuit, main circuit main
module main (
  input  [3:0] in,
  input  clock,
  output [3:0] out
);

  D_Flip_Flop #(.trigger("falling")) d_ff_1 (.clk(clock), .D(in[0]), .Q(out[0]));  // open: Qn, preset, en, reset
  D_Flip_Flop #(.trigger("falling")) d_ff_2 (.clk(clock), .D(in[1]), .Q(out[1]));  // open: Qn, preset, en, reset
  D_Flip_Flop #(.trigger("falling")) d_ff_3 (.clk(clock), .D(in[2]), .Q(out[2]));  // open: Qn, preset, en, reset
  D_Flip_Flop #(.trigger("falling")) d_ff_4 (.clk(clock), .D(in[3]), .Q(out[3]));  // open: Qn, preset, en, reset

  // Notes on the sheet:
  //   PIPO Register
endmodule
