// Logisim project counter4bit.circ as structural Verilog: 1 circuit, main circuit main
module main (
  input  clk,
  input  clear,
  output [3:0] out_3
);

  T_Flip_Flop #(.trigger("falling")) t_ff_1 (.clk(clk), .T(1'b1), .Q(out_3[0]), .reset(clear));  // open: Qn, preset, en
  T_Flip_Flop #(.trigger("falling")) t_ff_2 (
    .clk(out_3[0]), .T(1'b1), .Q(out_3[1]), .reset(clear));  // open: Qn, preset, en
  T_Flip_Flop #(.trigger("falling")) t_ff_3 (
    .clk(out_3[1]), .T(1'b1), .Q(out_3[2]), .reset(clear));  // open: Qn, preset, en
  T_Flip_Flop #(.trigger("falling")) t_ff_4 (
    .clk(out_3[2]), .T(1'b1), .Q(out_3[3]), .reset(clear));  // open: Qn, preset, en

  // Notes on the sheet:
  //   4 bit counter
endmodule
