// Logisim project parellelAdder.circ as structural Verilog: 1 circuit, main circuit main
module main (
  output carry,
  output [3:0] B,
  output [3:0] A,
  output [3:0] Sum
);

  wire A_in_out, Add_out, B_in_out, clear_out, clock_out;
  wire [3:0] counter_2_out_3, counter_out_3, multiplexer_1_out;

  Clock clock (.out(clock_out));
  Button B_in (.out(B_in_out));
  Button clear (.out(clear_out));
  Button A_in (.out(A_in_out));
  counter4bit_main counter (.clk(B_in_out), .clear(clear_out), .out_3(counter_out_3));
  counter4bit_main counter_2 (.clk(A_in_out), .clear(clear_out), .out_3(counter_2_out_3));
  Button Add (.out(Add_out));
  Multiplexer #(.width(4), .disabled(0), .enable("false")) multiplexer_1 (
    .in0(counter_out_3), .in1(Sum), .out(multiplexer_1_out), .sel(Add_out));
  PIPOresistor4bit_main PIPO_4_bit (.in(multiplexer_1_out), .clock(clock_out), .out(B));
  PIPOresistor4bit_main PIPO_4bit (.in(counter_2_out_3), .clock(clock_out), .out(A));
  _4bit_full_adder_main _4bit_parallel_adder (.B(B), .A(A), .S0(Sum), .Carry(carry));

  // Notes on the sheet:
  //   Parallel adder using registers and counters
endmodule
