// Logisim project counter01.circ as structural Verilog: 1 circuit, main circuit main
module main (
  input  clk,
  input  start,
  output o1,
  output o2
);

  T_Flip_Flop #(.trigger("falling")) t_ff_1 (.clk(clk), .T(start), .Q(o1));  // open: Qn, preset, reset, en
  T_Flip_Flop #(.trigger("falling")) t_ff_2 (.clk(o1), .T(start), .Q(o2));  // open: Qn, preset, reset, en

  // Notes on the sheet:
  //   2 bit counter
endmodule
