// Logisim project fulladder.circ as structural Verilog: 1 circuit, main circuit main
module main (
  input  I1,
  input  I2,
  input  carry,
  output Sum,
  output carry_2
);

  wire main_1_out_3, nand_1_out, nand_2_out;

  XOR_NAND_main main_1 (.in_1(I1), .in_2(I2), .out_3(main_1_out_3));
  nand nand_1 (nand_1_out, I1, I2);
  XOR_NAND_main main_2 (.in_1(main_1_out_3), .in_2(carry), .out_3(Sum));
  nand nand_2 (nand_2_out, carry, main_1_out_3);
  nand nand_3 (carry_2, nand_2_out, nand_1_out);

  // Notes on the sheet:
  //   Full Adder Cuicuit
endmodule
