// Logisim project serial_adder.circ as structural Verilog: 1 circuit, main circuit main
module main (
  input  [3:0] Input_A,
  input  [3:0] Input_B,
  input  start,
  output [4:0] SUM
);

  wire Clock_out, full_adder_carry_2, full_adder_sum, multiplexer_1_out, multiplexer_2_out, SISO_4bit_2_out,
       SISO_4bit_out;
  wire [1:0] counter_o1;

  Clock #(.highDuration(2), .lowDuration(2)) Clock (.out(Clock_out));
  counter01_main counter (.clk(Clock_out), .start(start), .o1(counter_o1[0]), .o2(counter_o1[1]));
  Multiplexer #(.select(2), .disabled(0), .enable("false")) multiplexer_1 (
    .in0(Input_A[0]), .in1(Input_A[1]), .in2(Input_A[2]), .in3(Input_A[3]), .out(multiplexer_1_out),
    .sel(counter_o1));
  Multiplexer #(.select(2), .disabled(0), .enable("false")) multiplexer_2 (
    .in0(Input_B[0]), .in1(Input_B[1]), .in2(Input_B[2]), .in3(Input_B[3]), .out(multiplexer_2_out),
    .sel(counter_o1));
  siso_4bit_main SISO_4bit (.clk(Clock_out), .in(multiplexer_1_out), .out(SISO_4bit_out));  // open: out_compliment
  siso_4bit_main SISO_4bit_2 (.clk(Clock_out), .in(multiplexer_2_out), .out(SISO_4bit_2_out));  // open: out_compliment
  fulladder_main full_adder (
    .I1(SISO_4bit_out), .I2(SISO_4bit_2_out), .carry(SUM[4]), .Sum(full_adder_sum),
    .carry_2(full_adder_carry_2));
  D_Flip_Flop #(.trigger("falling")) d_ff_1 (
    .clk(Clock_out), .D(full_adder_carry_2), .Q(SUM[4]));  // open: Qn, preset, en, reset
  sipo_4bit__main SIPO_4bit (.clk(Clock_out), .in(full_adder_sum), .o4(SUM[3]), ._03(SUM[2]), .o2(SUM[1]), .o1(SUM[0]));

  // Notes on the sheet:
  //   Serial Adder circuit using shift registers to take inputs to adder
endmodule
