// Logisim project sipo-4bit .circ as structural Verilog: 1 circuit, main circuit main
module main (
  input  clk,
  input  in,
  output o4,
  output _03,
  output o2,
  output o1
);

  D_Flip_Flop #(.trigger("falling")) d_ff_1 (.clk(clk), .D(in), .Q(o4));  // open: Qn, preset, en, reset
  D_Flip_Flop #(.trigger("falling")) d_ff_2 (.clk(clk), .D(o4), .Q(_03));  // open: Qn, preset, en, reset
  D_Flip_Flop #(.trigger("falling")) d_ff_3 (.clk(clk), .D(_03), .Q(o2));  // open: Qn, preset, en, reset
  D_Flip_Flop #(.trigger("falling")) d_ff_4 (.clk(clk), .D(o2), .Q(o1));  // open: Qn, preset, en, reset

  // Notes on the sheet:
  //   SIPO Register
endmodule
