// Logisim project siso-4bit.circ as structural Verilog: 1 circuit, main circuit main
module main (
  input  clk,
  input  in,
  output out,
  output out_compliment
);

  wire d_ff_1_q, d_ff_2_q, d_ff_3_q;

  D_Flip_Flop #(.trigger("falling")) d_ff_1 (.clk(clk), .D(in), .Q(d_ff_1_q));  // open: Qn, preset, en, reset
  D_Flip_Flop #(.trigger("falling")) d_ff_2 (.clk(clk), .D(d_ff_1_q), .Q(d_ff_2_q));  // open: Qn, preset, en, reset
  D_Flip_Flop #(.trigger("falling")) d_ff_3 (.clk(clk), .D(d_ff_2_q), .Q(d_ff_3_q));  // open: Qn, preset, en, reset
  D_Flip_Flop #(.trigger("falling")) d_ff_4 (
    .clk(clk), .D(d_ff_3_q), .Q(out), .Qn(out_compliment));  // open: preset, en, reset

  // Notes on the sheet:
  //   SISO Register
endmodule
