// Logisim project odd_parity.circ as structural Verilog: 1 circuit, main circuit main
module main (
  input  A,
  input  B,
  input  C,
  output P
);

  wire main_1_out_3, main_2_out_3;

  XOR_NAND_main main_1 (.in_1(A), .in_2(B), .out_3(main_1_out_3));
  XOR_NAND_main main_2 (.in_1(main_1_out_3), .in_2(C), .out_3(main_2_out_3));
  nand nand_1 (P, main_2_out_3, main_2_out_3);
endmodule
