// Logisim project 001910501060_RahulManna_Up-down_decade_counter.circ as structural Verilog: 1 circuit, main circuit main
module main (
  input  Control__0_up_1_down,
  output [3:0] OUTPUT
);

  wire and_1_out, and_2_out, and_3_out, and_4_out, and_5_out, and_6_out, and_7_out, and_8_out, and_9_out,
       and_10_out, and_11_out, Clock_out, FF0_qn, FF1_qn, FF2_qn, FF3_qn, not_1_out, or_1_out, or_2_out,
       or_3_out, or_4_out, or_5_out, or_6_out, or_7_out, or_8_out, Set_to_0_out, Set_to_9_out;

  Clock Clock (.out(Clock_out));
  Button Set_to_9 (.out(Set_to_9_out));
  J_K_Flip_Flop #(.trigger("falling")) FF3 (
    .J(or_2_out), .clk(Clock_out), .K(or_3_out), .Q(OUTPUT[3]), .Qn(FF3_qn), .preset(Set_to_9_out),
    .reset(Set_to_0_out));  // open: en
  J_K_Flip_Flop #(.trigger("falling")) FF2 (
    .J(or_4_out), .clk(Clock_out), .K(or_5_out), .Q(OUTPUT[2]), .Qn(FF2_qn), .reset(or_1_out));  // open: preset, en
  J_K_Flip_Flop #(.trigger("falling")) FF1 (
    .J(or_7_out), .clk(Clock_out), .K(or_8_out), .Q(OUTPUT[1]), .Qn(FF1_qn), .reset(or_1_out));  // open: preset, en
  J_K_Flip_Flop #(.trigger("falling")) FF0 (
    .J(1'b1), .clk(Clock_out), .K(1'b1), .Q(OUTPUT[0]), .Qn(FF0_qn), .preset(Set_to_9_out),
    .reset(Set_to_0_out));  // open: en
  or or_1 (or_1_out, Set_to_9_out, Set_to_0_out);
  not not_1 (not_1_out, Control__0_up_1_down);
  Button Set_to_0 (.out(Set_to_0_out));
  and and_1 (and_1_out, OUTPUT[0], not_1_out);
  and and_2 (and_2_out, OUTPUT[1], OUTPUT[2]);
  and and_3 (and_3_out, and_1_out, and_2_out);
  and and_4 (and_4_out, FF2_qn, FF1_qn);
  and and_5 (and_5_out, Control__0_up_1_down, FF0_qn);
  and and_6 (and_6_out, and_5_out, and_4_out);
  or or_2 (or_2_out, and_3_out, and_6_out);
  or or_3 (or_3_out, and_1_out, and_5_out);
  and and_7 (and_7_out, and_1_out, OUTPUT[1]);
  or or_4 (or_4_out, and_7_out, and_8_out);
  and and_8 (and_8_out, OUTPUT[3], and_5_out);
  and and_9 (and_9_out, and_5_out, FF1_qn);
  or or_5 (or_5_out, and_7_out, and_9_out);
  or or_6 (or_6_out, OUTPUT[2], OUTPUT[3]);
  and and_10 (and_10_out, or_6_out, and_5_out);
  or or_7 (or_7_out, and_10_out, and_11_out);
  // Probe on OUTPUT
  Hex_Digit_Display hex_digit_display_1 (.value(OUTPUT));  // open: dp
  and and_11 (and_11_out, and_1_out, FF3_qn);
  or or_8 (or_8_out, and_1_out, and_5_out);

  // Notes on the sheet:
  //   Up-Down Decade Counter Using JK FlipFlops
endmodule
