// Logisim project 001910501060_RahulManna_Cascaded_Decade_Counters_0-99.circ as structural Verilog: 3 circuits, main circuit main
module main (
  input  Down
);

  wire _0_out, _7SegmentDisplayDecoder_2_a, _7SegmentDisplayDecoder_2_b, _7SegmentDisplayDecoder_2_c,
       _7SegmentDisplayDecoder_2_d, _7SegmentDisplayDecoder_2_e, _7SegmentDisplayDecoder_2_f,
       _7SegmentDisplayDecoder_2_g, _7SegmentDisplayDecoder_a, _7SegmentDisplayDecoder_b,
       _7SegmentDisplayDecoder_c, _7SegmentDisplayDecoder_d, _7SegmentDisplayDecoder_e,
       _7SegmentDisplayDecoder_f, _7SegmentDisplayDecoder_g, and_1_out, and_2_out, and_3_out, and_4_out,
       clock_out, not_1_out, not_2_out, not_3_out, not_4_out, not_5_out, not_6_out, not_7_out, or_1_out;
  wire [3:0] UpDownDecadeCounter_2_output, UpDownDecadeCounter_output;

  and and_1 (and_1_out, and_3_out, Down);
  or or_1 (or_1_out, and_1_out, and_2_out);
  and and_2 (and_2_out, not_1_out, and_4_out);
  not not_1 (not_1_out, Down);
  Clock clock (.out(clock_out));
  Button _0 (.out(_0_out));
  and and_3 (and_3_out, not_2_out, not_3_out, not_4_out, not_5_out);
  and and_4 (and_4_out, UpDownDecadeCounter_2_output[0], not_6_out, not_7_out, UpDownDecadeCounter_2_output[3]);
  UpDownDecadeCounter UpDownDecadeCounter (
    .Control__0_up_1_down(Down), .Clock(or_1_out), .reset(_0_out), .OUTPUT(UpDownDecadeCounter_output));
  UpDownDecadeCounter UpDownDecadeCounter_2 (
    .Control__0_up_1_down(Down), .Clock(clock_out), .reset(_0_out), .OUTPUT(UpDownDecadeCounter_2_output));
  not not_2 (not_2_out, UpDownDecadeCounter_2_output[0]);
  not not_3 (not_3_out, UpDownDecadeCounter_2_output[1]);
  not not_4 (not_4_out, UpDownDecadeCounter_2_output[2]);
  not not_5 (not_5_out, UpDownDecadeCounter_2_output[3]);
  not not_6 (not_6_out, UpDownDecadeCounter_2_output[1]);
  not not_7 (not_7_out, UpDownDecadeCounter_2_output[2]);
  _7SegmentDisplayDecoder _7SegmentDisplayDecoder (
    .in_1(UpDownDecadeCounter_output), .a(_7SegmentDisplayDecoder_a), .b(_7SegmentDisplayDecoder_b),
    .c(_7SegmentDisplayDecoder_c), .d(_7SegmentDisplayDecoder_d), .e(_7SegmentDisplayDecoder_e),
    .f(_7SegmentDisplayDecoder_f), .g(_7SegmentDisplayDecoder_g));
  _7SegmentDisplayDecoder _7SegmentDisplayDecoder_2 (
    .in_1(UpDownDecadeCounter_2_output), .a(_7SegmentDisplayDecoder_2_a), .b(_7SegmentDisplayDecoder_2_b),
    .c(_7SegmentDisplayDecoder_2_c), .d(_7SegmentDisplayDecoder_2_d), .e(_7SegmentDisplayDecoder_2_e),
    .f(_7SegmentDisplayDecoder_2_f), .g(_7SegmentDisplayDecoder_2_g));
  _7_Segment_Display u_7_segment_display_1 (
    .g(_7SegmentDisplayDecoder_2_g), .f(_7SegmentDisplayDecoder_2_f), .a(_7SegmentDisplayDecoder_2_a),
    .b(_7SegmentDisplayDecoder_2_b), .e(_7SegmentDisplayDecoder_2_e), .d(_7SegmentDisplayDecoder_2_d),
    .c(_7SegmentDisplayDecoder_2_c));  // open: dp
  _7_Segment_Display u_7_segment_display_2 (
    .g(_7SegmentDisplayDecoder_g), .f(_7SegmentDisplayDecoder_f), .a(_7SegmentDisplayDecoder_a),
    .b(_7SegmentDisplayDecoder_b), .e(_7SegmentDisplayDecoder_e), .d(_7SegmentDisplayDecoder_d),
    .c(_7SegmentDisplayDecoder_c));  // open: dp
endmodule

module UpDownDecadeCounter (
  input  Control__0_up_1_down,
  input  Clock,
  input  reset,
  output [3:0] OUTPUT
);

  wire and_1_out, and_2_out, and_3_out, and_4_out, and_5_out, and_6_out, and_7_out, and_8_out, and_9_out,
       and_10_out, and_11_out, FF0_qn, FF1_qn, FF2_qn, FF3_qn, not_1_out, or_1_out, or_2_out, or_3_out,
       or_4_out, or_5_out, or_6_out, or_7_out;

  J_K_Flip_Flop #(.trigger("falling")) FF3 (
    .J(or_1_out), .clk(Clock), .K(or_2_out), .Q(OUTPUT[3]), .Qn(FF3_qn), .reset(reset));  // open: preset, en
  J_K_Flip_Flop #(.trigger("falling")) FF2 (
    .J(or_3_out), .clk(Clock), .K(or_4_out), .Q(OUTPUT[2]), .Qn(FF2_qn), .reset(reset));  // open: preset, en
  J_K_Flip_Flop #(.trigger("falling")) FF1 (
    .J(or_6_out), .clk(Clock), .K(or_7_out), .Q(OUTPUT[1]), .Qn(FF1_qn), .reset(reset));  // open: preset, en
  J_K_Flip_Flop #(.trigger("falling")) FF0 (
    .J(1'b1), .clk(Clock), .K(1'b1), .Q(OUTPUT[0]), .Qn(FF0_qn), .reset(reset));  // open: preset, en
  not not_1 (not_1_out, Control__0_up_1_down);
  and and_1 (and_1_out, OUTPUT[0], not_1_out);
  and and_2 (and_2_out, OUTPUT[1], OUTPUT[2]);
  and and_3 (and_3_out, and_1_out, and_2_out);
  and and_4 (and_4_out, FF2_qn, FF1_qn);
  and and_5 (and_5_out, Control__0_up_1_down, FF0_qn);
  and and_6 (and_6_out, and_5_out, and_4_out);
  or or_1 (or_1_out, and_3_out, and_6_out);
  or or_2 (or_2_out, and_1_out, and_5_out);
  and and_7 (and_7_out, and_1_out, OUTPUT[1]);
  or or_3 (or_3_out, and_7_out, and_9_out);
  and and_8 (and_8_out, and_5_out, FF1_qn);
  and and_9 (and_9_out, OUTPUT[3], and_5_out);
  or or_4 (or_4_out, and_7_out, and_8_out);
  or or_5 (or_5_out, OUTPUT[2], OUTPUT[3]);
  and and_10 (and_10_out, or_5_out, and_5_out);
  or or_6 (or_6_out, and_10_out, and_11_out);
  // Probe on OUTPUT
  Hex_Digit_Display hex_digit_display_1 (.value(OUTPUT));  // open: dp
  and and_11 (and_11_out, and_1_out, FF3_qn);
  or or_7 (or_7_out, and_1_out, and_5_out);

  // Notes on the sheet:
  //   Up-Down Decade Counter Using JK FlipFlops
endmodule

module _7SegmentDisplayDecoder (
  input  [3:0] in_1,
  output a,
  output b,
  output c,
  output d,
  output e,
  output f,
  output g
);

  wire and_1_out, and_2_out, and_3_out, and_4_out, and_5_out, and_6_out, and_7_out, and_8_out, and_9_out,
       and_10_out, and_11_out, and_12_out, and_13_out, and_14_out, and_15_out, and_16_out, and_17_out,
       not_1_out, not_2_out, not_3_out, not_4_out, not_5_out, not_6_out, not_7_out, not_8_out, not_9_out,
       not_10_out, not_11_out, not_12_out, not_13_out, not_14_out, not_15_out, not_16_out, not_17_out,
       not_18_out, not_19_out, not_20_out, not_21_out, or_1_out, or_2_out, or_3_out, or_4_out, or_6_out,
       or_8_out, or_9_out, or_10_out, or_11_out, or_14_out, or_15_out;

  not not_1 (not_1_out, in_1[2]);
  not not_2 (not_2_out, in_1[0]);
  not not_3 (not_3_out, in_1[1]);
  not not_4 (not_4_out, in_1[0]);
  not not_5 (not_5_out, in_1[1]);
  not not_6 (not_6_out, in_1[2]);
  not not_7 (not_7_out, in_1[0]);
  not not_8 (not_8_out, in_1[2]);
  not not_9 (not_9_out, in_1[1]);
  not not_10 (not_10_out, in_1[2]);
  not not_11 (not_11_out, in_1[0]);
  not not_12 (not_12_out, in_1[0]);
  not not_13 (not_13_out, in_1[1]);
  not not_14 (not_14_out, in_1[0]);
  not not_15 (not_15_out, in_1[1]);
  not not_16 (not_16_out, in_1[0]);
  not not_17 (not_17_out, in_1[2]);
  not not_18 (not_18_out, in_1[1]);
  not not_19 (not_19_out, in_1[0]);
  and and_1 (and_1_out, not_1_out, not_2_out);
  and and_2 (and_2_out, in_1[2], in_1[0]);
  not not_20 (not_20_out, in_1[2]);
  and and_3 (and_3_out, not_3_out, not_4_out);
  or or_1 (or_1_out, not_5_out, in_1[0]);
  and and_4 (and_4_out, not_6_out, not_7_out);
  and and_5 (and_5_out, not_8_out, in_1[1]);
  not not_21 (not_21_out, in_1[0]);
  and and_6 (and_6_out, in_1[2], not_9_out);
  and and_7 (and_7_out, not_10_out, not_11_out);
  and and_8 (and_8_out, in_1[1], not_12_out);
  and and_9 (and_9_out, not_13_out, not_14_out);
  and and_10 (and_10_out, in_1[2], not_15_out);
  and and_11 (and_11_out, in_1[2], not_16_out);
  and and_12 (and_12_out, not_17_out, in_1[1]);
  and and_13 (and_13_out, in_1[2], not_18_out);
  and and_14 (and_14_out, in_1[2], not_19_out);
  or or_2 (or_2_out, and_1_out, in_1[1]);
  or or_3 (or_3_out, and_2_out, in_1[3]);
  or or_4 (or_4_out, not_20_out, and_3_out);
  and and_15 (and_15_out, in_1[1], in_1[0]);
  or or_5 (c, or_1_out, in_1[2]);
  or or_6 (or_6_out, and_4_out, and_5_out);
  and and_16 (and_16_out, in_1[1], not_21_out);
  and and_17 (and_17_out, and_6_out, in_1[0]);
  or or_7 (e, and_7_out, and_8_out);
  or or_8 (or_8_out, and_9_out, and_10_out);
  or or_9 (or_9_out, and_11_out, in_1[3]);
  or or_10 (or_10_out, and_12_out, and_13_out);
  or or_11 (or_11_out, and_14_out, in_1[3]);
  or or_12 (a, or_2_out, or_3_out);
  or or_13 (b, or_4_out, and_15_out);
  or or_14 (or_14_out, or_6_out, and_16_out);
  or or_15 (or_15_out, and_17_out, in_1[3]);
  or or_16 (f, or_8_out, or_9_out);
  or or_17 (g, or_10_out, or_11_out);
  or or_18 (d, or_14_out, or_15_out);
  _7_Segment_Display u_7_segment_display_1 (.g(g), .f(f), .a(a), .b(b), .e(e), .d(d), .c(c));  // open: dp
endmodule
