// Logisim project 001910501060_RahulManna_0-59_up_counter.circ as structural Verilog: 4 circuits, main circuit main
module main (
);

  wire _7_SEG_DISP_ENCODER_2_a, _7_SEG_DISP_ENCODER_2_b, _7_SEG_DISP_ENCODER_2_c, _7_SEG_DISP_ENCODER_2_d,
       _7_SEG_DISP_ENCODER_2_e, _7_SEG_DISP_ENCODER_2_f, _7_SEG_DISP_ENCODER_2_g, _7_SEG_DISP_ENCODER_a,
       _7_SEG_DISP_ENCODER_b, _7_SEG_DISP_ENCODER_c, _7_SEG_DISP_ENCODER_d, _7_SEG_DISP_ENCODER_e,
       _7_SEG_DISP_ENCODER_f, _7_SEG_DISP_ENCODER_g, and_1_out, clock_out, not_1_out, not_2_out, Reset_out;
  wire [3:0] MOD_6_out, MOD_10_out;

  Clock clock (.out(clock_out));
  Button Reset (.out(Reset_out));
  and and_1 (and_1_out, MOD_10_out[3], not_1_out, not_2_out, MOD_10_out[0]);
  MOD_6_up_counter MOD_6 (.Clock(and_1_out), .Reset(Reset_out), .OUT(MOD_6_out));
  MOD10_up_counter MOD_10 (.Clock(clock_out), .Reset(Reset_out), .OUT(MOD_10_out));
  not not_1 (not_1_out, MOD_10_out[2]);
  not not_2 (not_2_out, MOD_10_out[1]);
  _7_SEG_DISP_ENCODER _7_SEG_DISP_ENCODER (
    .in_1(MOD_6_out), .a(_7_SEG_DISP_ENCODER_a), .b(_7_SEG_DISP_ENCODER_b), .c(_7_SEG_DISP_ENCODER_c),
    .d(_7_SEG_DISP_ENCODER_d), .e(_7_SEG_DISP_ENCODER_e), .f(_7_SEG_DISP_ENCODER_f), .g(_7_SEG_DISP_ENCODER_g));
  _7_SEG_DISP_ENCODER _7_SEG_DISP_ENCODER_2 (
    .in_1(MOD_10_out), .a(_7_SEG_DISP_ENCODER_2_a), .b(_7_SEG_DISP_ENCODER_2_b), .c(_7_SEG_DISP_ENCODER_2_c),
    .d(_7_SEG_DISP_ENCODER_2_d), .e(_7_SEG_DISP_ENCODER_2_e), .f(_7_SEG_DISP_ENCODER_2_f),
    .g(_7_SEG_DISP_ENCODER_2_g));
  _7_Segment_Display u_7_segment_display_1 (
    .g(_7_SEG_DISP_ENCODER_2_g), .f(_7_SEG_DISP_ENCODER_2_f), .a(_7_SEG_DISP_ENCODER_2_a),
    .b(_7_SEG_DISP_ENCODER_2_b), .e(_7_SEG_DISP_ENCODER_2_e), .d(_7_SEG_DISP_ENCODER_2_d),
    .c(_7_SEG_DISP_ENCODER_2_c));  // open: dp
  _7_Segment_Display u_7_segment_display_2 (
    .g(_7_SEG_DISP_ENCODER_g), .f(_7_SEG_DISP_ENCODER_f), .a(_7_SEG_DISP_ENCODER_a),
    .b(_7_SEG_DISP_ENCODER_b), .e(_7_SEG_DISP_ENCODER_e), .d(_7_SEG_DISP_ENCODER_d), .c(_7_SEG_DISP_ENCODER_c));  // open: dp

  // Notes on the sheet:
  //   0-59 up counter
endmodule

module MOD10_up_counter (
  input  Clock,
  input  Reset,
  output [3:0] OUT
);

  wire and_1_out, and_2_out, and_3_out, FF3_qn;

  J_K_Flip_Flop #(.trigger("falling")) FF3 (
    .J(and_3_out), .clk(Clock), .K(OUT[0]), .Q(OUT[3]), .Qn(FF3_qn), .reset(Reset));  // open: preset, en
  J_K_Flip_Flop #(.trigger("falling")) FF2 (
    .J(and_2_out), .clk(Clock), .K(and_2_out), .Q(OUT[2]), .reset(Reset));  // open: Qn, preset, en
  J_K_Flip_Flop #(.trigger("falling")) FF1 (
    .J(and_1_out), .clk(Clock), .K(OUT[0]), .Q(OUT[1]), .reset(Reset));  // open: Qn, preset, en
  J_K_Flip_Flop #(.trigger("falling")) FF0 (
    .J(1'b1), .clk(Clock), .K(1'b1), .Q(OUT[0]), .reset(Reset));  // open: Qn, preset, en
  and and_1 (and_1_out, OUT[0], FF3_qn);
  and and_2 (and_2_out, OUT[0], OUT[1]);
  and and_3 (and_3_out, and_2_out, OUT[2]);
  // Probe on OUT

  // Notes on the sheet:
  //   Mod10 up counter
endmodule

module MOD_6_up_counter (
  input  Clock,
  input  Reset,
  output [3:0] OUT
);

  wire and_1_out, and_2_out, FF2_qn;

  J_K_Flip_Flop #(.trigger("falling")) FF2 (
    .J(and_2_out), .clk(Clock), .K(OUT[0]), .Q(OUT[2]), .Qn(FF2_qn), .reset(Reset));  // open: preset, en
  J_K_Flip_Flop #(.trigger("falling")) FF1 (
    .J(and_1_out), .clk(Clock), .K(OUT[0]), .Q(OUT[1]), .reset(Reset));  // open: Qn, preset, en
  J_K_Flip_Flop #(.trigger("falling")) FF0 (
    .J(1'b1), .clk(Clock), .K(1'b1), .Q(OUT[0]), .reset(Reset));  // open: Qn, preset, en
  and and_1 (and_1_out, OUT[0], FF2_qn);
  and and_2 (and_2_out, OUT[0], OUT[1]);
  not not_1 (OUT[3], 1'b1);
  // Probe on OUT

  // Notes on the sheet:
  //   Mod6 up counter
endmodule

module _7_SEG_DISP_ENCODER (
  input  [3:0] in_1,
  output a,
  output b,
  output c,
  output d,
  output e,
  output f,
  output g
);

  wire and_1_out, and_2_out, and_3_out, and_4_out, and_5_out, and_6_out, and_7_out, and_8_out, and_9_out,
       and_10_out, and_11_out, and_12_out, and_13_out, and_14_out, and_15_out, and_16_out, and_17_out,
       not_1_out, not_2_out, not_3_out, not_4_out, not_5_out, not_6_out, not_7_out, not_8_out, not_9_out,
       not_10_out, not_11_out, not_12_out, not_13_out, not_14_out, not_15_out, not_16_out, not_17_out,
       not_18_out, not_19_out, not_20_out, not_21_out, or_1_out, or_2_out, or_3_out, or_4_out, or_6_out,
       or_8_out, or_9_out, or_10_out, or_11_out, or_14_out, or_15_out;

  not not_1 (not_1_out, in_1[2]);
  not not_2 (not_2_out, in_1[0]);
  not not_3 (not_3_out, in_1[1]);
  not not_4 (not_4_out, in_1[0]);
  not not_5 (not_5_out, in_1[1]);
  not not_6 (not_6_out, in_1[2]);
  not not_7 (not_7_out, in_1[0]);
  not not_8 (not_8_out, in_1[2]);
  not not_9 (not_9_out, in_1[1]);
  not not_10 (not_10_out, in_1[2]);
  not not_11 (not_11_out, in_1[0]);
  not not_12 (not_12_out, in_1[0]);
  not not_13 (not_13_out, in_1[1]);
  not not_14 (not_14_out, in_1[0]);
  not not_15 (not_15_out, in_1[1]);
  not not_16 (not_16_out, in_1[0]);
  not not_17 (not_17_out, in_1[2]);
  not not_18 (not_18_out, in_1[1]);
  not not_19 (not_19_out, in_1[0]);
  and and_1 (and_1_out, not_1_out, not_2_out);
  and and_2 (and_2_out, in_1[2], in_1[0]);
  not not_20 (not_20_out, in_1[2]);
  and and_3 (and_3_out, not_3_out, not_4_out);
  or or_1 (or_1_out, not_5_out, in_1[0]);
  and and_4 (and_4_out, not_6_out, not_7_out);
  and and_5 (and_5_out, not_8_out, in_1[1]);
  not not_21 (not_21_out, in_1[0]);
  and and_6 (and_6_out, in_1[2], not_9_out);
  and and_7 (and_7_out, not_10_out, not_11_out);
  and and_8 (and_8_out, in_1[1], not_12_out);
  and and_9 (and_9_out, not_13_out, not_14_out);
  and and_10 (and_10_out, in_1[2], not_15_out);
  and and_11 (and_11_out, in_1[2], not_16_out);
  and and_12 (and_12_out, not_17_out, in_1[1]);
  and and_13 (and_13_out, in_1[2], not_18_out);
  and and_14 (and_14_out, in_1[2], not_19_out);
  or or_2 (or_2_out, and_1_out, in_1[1]);
  or or_3 (or_3_out, and_2_out, in_1[3]);
  or or_4 (or_4_out, not_20_out, and_3_out);
  and and_15 (and_15_out, in_1[1], in_1[0]);
  or or_5 (c, or_1_out, in_1[2]);
  or or_6 (or_6_out, and_4_out, and_5_out);
  and and_16 (and_16_out, in_1[1], not_21_out);
  and and_17 (and_17_out, and_6_out, in_1[0]);
  or or_7 (e, and_7_out, and_8_out);
  or or_8 (or_8_out, and_9_out, and_10_out);
  or or_9 (or_9_out, and_11_out, in_1[3]);
  or or_10 (or_10_out, and_12_out, and_13_out);
  or or_11 (or_11_out, and_14_out, in_1[3]);
  or or_12 (a, or_2_out, or_3_out);
  or or_13 (b, or_4_out, and_15_out);
  or or_14 (or_14_out, or_6_out, and_16_out);
  or or_15 (or_15_out, and_17_out, in_1[3]);
  or or_16 (f, or_8_out, or_9_out);
  or or_17 (g, or_10_out, or_11_out);
  or or_18 (d, or_14_out, or_15_out);
  _7_Segment_Display u_7_segment_display_1 (.g(g), .f(f), .a(a), .b(b), .e(e), .d(d), .c(c));  // open: dp
endmodule
