// Logisim project 001910501060_RahulManna_Clock_24hr.circ as structural Verilog: 6 circuits, main circuit main
module main (
  input  Pause,
  input  [3:0] H_10_s_place,
  input  [3:0] H_1_s_place,
  input  [3:0] M_10_s_place,
  input  [3:0] M_1_s_place,
  input  [3:0] S_10_s_place,
  input  [3:0] S_1_s_place
);

  wire and_1_out, and_2_out, Clock_out, Load_out, not_1_out, not_2_out, not_3_out, not_4_out, or_1_out,
       Reset_out;
  wire [3:0] HH__1_s_place, HH__10_s_place, MM__1_s_place, MM__10_s_place, SS__1_s_place, SS__10_s_place;

  Button Load (.out(Load_out));
  Clock Clock (.out(Clock_out));
  Button Reset (.out(Reset_out));
  or or_1 (or_1_out, Clock_out, Pause);
  _0_23_counter HH (
    .Load(Load_out), .Clock(and_1_out), .Reset(Reset_out), .set_10_s_place(H_10_s_place),
    .set_1_s_place(H_1_s_place), ._10_s_place(HH__10_s_place), ._1_s_place(HH__1_s_place));
  Hex_Digit_Display hex_digit_display_1 (.value(HH__1_s_place));  // open: dp
  Hex_Digit_Display hex_digit_display_2 (.value(HH__10_s_place));  // open: dp
  and and_1 (and_1_out, not_1_out, MM__10_s_place[2], not_2_out, MM__10_s_place[0]);
  Hex_Digit_Display hex_digit_display_3 (.value(MM__10_s_place));  // open: dp
  _0_59_counter MM (
    .Load(Load_out), .Clock(and_2_out), .Reset(Reset_out), .set_10_s_place(M_10_s_place),
    .set_1_s_place(M_1_s_place), ._10_s_place(MM__10_s_place), ._1_s_place(MM__1_s_place));
  not not_1 (not_1_out, MM__10_s_place[3]);
  not not_2 (not_2_out, MM__10_s_place[1]);
  Hex_Digit_Display hex_digit_display_4 (.value(MM__1_s_place));  // open: dp
  and and_2 (and_2_out, not_3_out, SS__10_s_place[2], not_4_out, SS__10_s_place[0]);
  Hex_Digit_Display hex_digit_display_5 (.value(SS__10_s_place));  // open: dp
  _0_59_counter SS (
    .Load(Load_out), .Clock(or_1_out), .Reset(Reset_out), .set_10_s_place(S_10_s_place),
    .set_1_s_place(S_1_s_place), ._10_s_place(SS__10_s_place), ._1_s_place(SS__1_s_place));
  not not_3 (not_3_out, SS__10_s_place[3]);
  not not_4 (not_4_out, SS__10_s_place[1]);
  Hex_Digit_Display hex_digit_display_6 (.value(SS__1_s_place));  // open: dp
  // Probe on H_10_s_place
  // Probe on H_1_s_place
  // Probe on M_10_s_place
  // Probe on M_1_s_place
  // Probe on S_10_s_place
  // Probe on S_1_s_place

  // Notes on the sheet:
  //   :
  //   :
endmodule

module MOD10_up_counter (
  input  Load,
  input  Clock,
  input  [3:0] Set_to,
  input  Reset,
  output [3:0] OUT
);

  wire and_1_out, and_2_out, and_3_out, and_4_out, and_5_out, and_6_out, and_7_out, and_8_out, and_9_out,
       and_10_out, and_11_out, FF3_qn, not_1_out, not_2_out, not_3_out, not_4_out, or_1_out, or_2_out,
       or_3_out, or_4_out;

  J_K_Flip_Flop #(.trigger("falling")) FF3 (
    .J(and_3_out), .clk(Clock), .K(OUT[0]), .Q(OUT[3]), .Qn(FF3_qn), .preset(and_4_out), .reset(or_1_out));  // open: en
  J_K_Flip_Flop #(.trigger("falling")) FF2 (
    .J(and_2_out), .clk(Clock), .K(and_2_out), .Q(OUT[2]), .preset(and_5_out), .reset(or_2_out));  // open: Qn, en
  J_K_Flip_Flop #(.trigger("falling")) FF0 (
    .J(and_1_out), .clk(Clock), .K(OUT[0]), .Q(OUT[1]), .preset(and_6_out), .reset(or_3_out));  // open: Qn, en
  J_K_Flip_Flop #(.trigger("falling")) FF0_2 (
    .J(1'b1), .clk(Clock), .K(1'b1), .Q(OUT[0]), .preset(and_7_out), .reset(or_4_out));  // open: Qn, en
  and and_1 (and_1_out, OUT[0], FF3_qn);
  and and_2 (and_2_out, OUT[0], OUT[1]);
  // Probe on OUT
  and and_3 (and_3_out, and_2_out, OUT[2]);
  or or_1 (or_1_out, Reset, and_8_out);
  and and_4 (and_4_out, Set_to[3], Load);
  or or_2 (or_2_out, Reset, and_9_out);
  and and_5 (and_5_out, Set_to[2], Load);
  or or_3 (or_3_out, Reset, and_10_out);
  and and_6 (and_6_out, Set_to[1], Load);
  or or_4 (or_4_out, Reset, and_11_out);
  and and_7 (and_7_out, Set_to[0], Load);
  and and_8 (and_8_out, Load, not_1_out);
  not not_1 (not_1_out, Set_to[3]);
  and and_9 (and_9_out, Load, not_2_out);
  not not_2 (not_2_out, Set_to[2]);
  and and_10 (and_10_out, Load, not_3_out);
  not not_3 (not_3_out, Set_to[1]);
  and and_11 (and_11_out, Load, not_4_out);
  not not_4 (not_4_out, Set_to[0]);

  // Notes on the sheet:
  //   Mod10 up counter
  //   with parallel loading
endmodule

module MOD_6_up_counter (
  input  Load,
  input  Clock,
  input  [3:0] Set_to,
  input  Reset,
  output [3:0] OUT
);

  wire and_1_out, and_2_out, and_3_out, and_4_out, and_5_out, and_6_out, and_7_out, and_8_out, FF2_qn,
       not_2_out, not_3_out, not_4_out, or_1_out, or_2_out, or_3_out;

  J_K_Flip_Flop #(.trigger("falling")) FF2 (
    .J(and_1_out), .clk(Clock), .K(OUT[0]), .Q(OUT[2]), .Qn(FF2_qn), .preset(and_3_out), .reset(or_1_out));  // open: en
  J_K_Flip_Flop #(.trigger("falling")) FF1 (
    .J(and_2_out), .clk(Clock), .K(OUT[0]), .Q(OUT[1]), .preset(and_4_out), .reset(or_2_out));  // open: Qn, en
  J_K_Flip_Flop #(.trigger("falling")) FF0 (
    .J(1'b1), .clk(Clock), .K(1'b1), .Q(OUT[0]), .preset(and_5_out), .reset(or_3_out));  // open: Qn, en
  and and_1 (and_1_out, OUT[0], OUT[1]);
  and and_2 (and_2_out, OUT[0], FF2_qn);
  not not_1 (OUT[3], 1'b1);
  // Probe on OUT
  or or_1 (or_1_out, Reset, and_6_out);
  and and_3 (and_3_out, Set_to[2], Load);
  or or_2 (or_2_out, Reset, and_7_out);
  and and_4 (and_4_out, Set_to[1], Load);
  or or_3 (or_3_out, Reset, and_8_out);
  and and_5 (and_5_out, Set_to[0], Load);
  and and_6 (and_6_out, Load, not_2_out);
  and and_7 (and_7_out, Load, not_3_out);
  and and_8 (and_8_out, Load, not_4_out);
  not not_2 (not_2_out, Set_to[2]);
  not not_3 (not_3_out, Set_to[1]);
  not not_4 (not_4_out, Set_to[0]);

  // Notes on the sheet:
  //   Mod 6 up counter
  //   with parallel loading
endmodule

module _7_SEG_DISP_ENCODER (
  input  [3:0] in_1,
  output a,
  output b,
  output c,
  output d,
  output e,
  output f,
  output g
);

  wire and_1_out, and_2_out, and_3_out, and_4_out, and_5_out, and_6_out, and_7_out, and_8_out, and_9_out,
       and_10_out, and_11_out, and_12_out, and_13_out, and_14_out, and_15_out, and_16_out, and_17_out,
       not_1_out, not_2_out, not_3_out, not_4_out, not_5_out, not_6_out, not_7_out, not_8_out, not_9_out,
       not_10_out, not_11_out, not_12_out, not_13_out, not_14_out, not_15_out, not_16_out, not_17_out,
       not_18_out, not_19_out, not_20_out, not_21_out, or_1_out, or_2_out, or_3_out, or_4_out, or_6_out,
       or_8_out, or_9_out, or_10_out, or_11_out, or_14_out, or_15_out;

  not not_1 (not_1_out, in_1[2]);
  not not_2 (not_2_out, in_1[0]);
  not not_3 (not_3_out, in_1[1]);
  not not_4 (not_4_out, in_1[0]);
  not not_5 (not_5_out, in_1[1]);
  not not_6 (not_6_out, in_1[2]);
  not not_7 (not_7_out, in_1[0]);
  not not_8 (not_8_out, in_1[2]);
  not not_9 (not_9_out, in_1[1]);
  not not_10 (not_10_out, in_1[2]);
  not not_11 (not_11_out, in_1[0]);
  not not_12 (not_12_out, in_1[0]);
  not not_13 (not_13_out, in_1[1]);
  not not_14 (not_14_out, in_1[0]);
  not not_15 (not_15_out, in_1[1]);
  not not_16 (not_16_out, in_1[0]);
  not not_17 (not_17_out, in_1[2]);
  not not_18 (not_18_out, in_1[1]);
  not not_19 (not_19_out, in_1[0]);
  and and_1 (and_1_out, not_1_out, not_2_out);
  and and_2 (and_2_out, in_1[2], in_1[0]);
  not not_20 (not_20_out, in_1[2]);
  and and_3 (and_3_out, not_3_out, not_4_out);
  or or_1 (or_1_out, not_5_out, in_1[0]);
  and and_4 (and_4_out, not_6_out, not_7_out);
  and and_5 (and_5_out, not_8_out, in_1[1]);
  not not_21 (not_21_out, in_1[0]);
  and and_6 (and_6_out, in_1[2], not_9_out);
  and and_7 (and_7_out, not_10_out, not_11_out);
  and and_8 (and_8_out, in_1[1], not_12_out);
  and and_9 (and_9_out, not_13_out, not_14_out);
  and and_10 (and_10_out, in_1[2], not_15_out);
  and and_11 (and_11_out, in_1[2], not_16_out);
  and and_12 (and_12_out, not_17_out, in_1[1]);
  and and_13 (and_13_out, in_1[2], not_18_out);
  and and_14 (and_14_out, in_1[2], not_19_out);
  or or_2 (or_2_out, and_1_out, in_1[1]);
  or or_3 (or_3_out, and_2_out, in_1[3]);
  or or_4 (or_4_out, not_20_out, and_3_out);
  and and_15 (and_15_out, in_1[1], in_1[0]);
  or or_5 (c, or_1_out, in_1[2]);
  or or_6 (or_6_out, and_4_out, and_5_out);
  and and_16 (and_16_out, in_1[1], not_21_out);
  and and_17 (and_17_out, and_6_out, in_1[0]);
  or or_7 (e, and_7_out, and_8_out);
  or or_8 (or_8_out, and_9_out, and_10_out);
  or or_9 (or_9_out, and_11_out, in_1[3]);
  or or_10 (or_10_out, and_12_out, and_13_out);
  or or_11 (or_11_out, and_14_out, in_1[3]);
  or or_12 (a, or_2_out, or_3_out);
  or or_13 (b, or_4_out, and_15_out);
  or or_14 (or_14_out, or_6_out, and_16_out);
  or or_15 (or_15_out, and_17_out, in_1[3]);
  or or_16 (f, or_8_out, or_9_out);
  or or_17 (g, or_10_out, or_11_out);
  or or_18 (d, or_14_out, or_15_out);
  _7_Segment_Display u_7_segment_display_1 (.g(g), .f(f), .a(a), .b(b), .e(e), .d(d), .c(c));  // open: dp
endmodule

module _0_59_counter (
  input  Load,
  input  Clock,
  input  Reset,
  input  [3:0] set_10_s_place,
  input  [3:0] set_1_s_place,
  output [3:0] _10_s_place,
  output [3:0] _1_s_place
);

  wire and_1_out, n7_seg_disp_encoder_1_a, n7_seg_disp_encoder_1_b, n7_seg_disp_encoder_1_c,
       n7_seg_disp_encoder_1_d, n7_seg_disp_encoder_1_e, n7_seg_disp_encoder_1_f, n7_seg_disp_encoder_1_g,
       n7_seg_disp_encoder_2_a, n7_seg_disp_encoder_2_b, n7_seg_disp_encoder_2_c, n7_seg_disp_encoder_2_d,
       n7_seg_disp_encoder_2_e, n7_seg_disp_encoder_2_f, n7_seg_disp_encoder_2_g, not_1_out, not_2_out;

  and and_1 (and_1_out, _1_s_place[3], not_1_out, not_2_out, _1_s_place[0]);
  MOD_6_up_counter MOD_6 (.Load(Load), .Clock(and_1_out), .Set_to(set_10_s_place), .Reset(Reset), .OUT(_10_s_place));
  MOD10_up_counter MOD_10 (.Load(Load), .Clock(Clock), .Set_to(set_1_s_place), .Reset(Reset), .OUT(_1_s_place));
  not not_1 (not_1_out, _1_s_place[2]);
  not not_2 (not_2_out, _1_s_place[1]);
  _7_SEG_DISP_ENCODER u_7_seg_disp_encoder_1 (
    .in_1(_10_s_place), .a(n7_seg_disp_encoder_1_a), .b(n7_seg_disp_encoder_1_b),
    .c(n7_seg_disp_encoder_1_c), .d(n7_seg_disp_encoder_1_d), .e(n7_seg_disp_encoder_1_e),
    .f(n7_seg_disp_encoder_1_f), .g(n7_seg_disp_encoder_1_g));
  _7_SEG_DISP_ENCODER u_7_seg_disp_encoder_2 (
    .in_1(_1_s_place), .a(n7_seg_disp_encoder_2_a), .b(n7_seg_disp_encoder_2_b), .c(n7_seg_disp_encoder_2_c),
    .d(n7_seg_disp_encoder_2_d), .e(n7_seg_disp_encoder_2_e), .f(n7_seg_disp_encoder_2_f),
    .g(n7_seg_disp_encoder_2_g));
  _7_Segment_Display u_7_segment_display_1 (
    .g(n7_seg_disp_encoder_1_g), .f(n7_seg_disp_encoder_1_f), .a(n7_seg_disp_encoder_1_a),
    .b(n7_seg_disp_encoder_1_b), .e(n7_seg_disp_encoder_1_e), .d(n7_seg_disp_encoder_1_d),
    .c(n7_seg_disp_encoder_1_c));  // open: dp
  _7_Segment_Display u_7_segment_display_2 (
    .g(n7_seg_disp_encoder_2_g), .f(n7_seg_disp_encoder_2_f), .a(n7_seg_disp_encoder_2_a),
    .b(n7_seg_disp_encoder_2_b), .e(n7_seg_disp_encoder_2_e), .d(n7_seg_disp_encoder_2_d),
    .c(n7_seg_disp_encoder_2_c));  // open: dp

  // Notes on the sheet:
  //   0-59 up counter
  //   with parallel loading
endmodule

module _0_23_counter (
  input  Load,
  input  Clock,
  input  Reset,
  input  [3:0] set_10_s_place,
  input  [3:0] set_1_s_place,
  output [3:0] _10_s_place,
  output [3:0] _1_s_place
);

  wire and_1_out, and_2_out, and_3_out, and_4_out, n7_seg_disp_encoder_1_a, n7_seg_disp_encoder_1_b,
       n7_seg_disp_encoder_1_c, n7_seg_disp_encoder_1_d, n7_seg_disp_encoder_1_e, n7_seg_disp_encoder_1_f,
       n7_seg_disp_encoder_1_g, n7_seg_disp_encoder_2_a, n7_seg_disp_encoder_2_b, n7_seg_disp_encoder_2_c,
       n7_seg_disp_encoder_2_d, n7_seg_disp_encoder_2_e, n7_seg_disp_encoder_2_f, n7_seg_disp_encoder_2_g,
       not_1_out, not_2_out, not_3_out, not_4_out, not_5_out, not_6_out, not_7_out, not_8_out, or_1_out;

  or or_1 (or_1_out, Reset, and_2_out);
  and and_1 (and_1_out, _1_s_place[3], not_1_out, not_2_out, _1_s_place[0]);
  and and_2 (and_2_out, and_3_out, and_4_out);
  MOD_6_up_counter MOD_6 (.Load(Load), .Clock(and_1_out), .Set_to(set_10_s_place), .Reset(or_1_out), .OUT(_10_s_place));
  MOD10_up_counter MOD_10 (.Load(Load), .Clock(Clock), .Set_to(set_1_s_place), .Reset(or_1_out), .OUT(_1_s_place));
  not not_1 (not_1_out, _1_s_place[2]);
  not not_2 (not_2_out, _1_s_place[1]);
  and and_3 (and_3_out, not_3_out, not_4_out, _10_s_place[1], not_5_out);
  not not_3 (not_3_out, _10_s_place[3]);
  not not_4 (not_4_out, _10_s_place[2]);
  not not_5 (not_5_out, _10_s_place[0]);
  and and_4 (and_4_out, not_6_out, _1_s_place[2], not_7_out, not_8_out);
  not not_6 (not_6_out, _1_s_place[3]);
  not not_7 (not_7_out, _1_s_place[1]);
  not not_8 (not_8_out, _1_s_place[0]);
  _7_SEG_DISP_ENCODER u_7_seg_disp_encoder_1 (
    .in_1(_10_s_place), .a(n7_seg_disp_encoder_1_a), .b(n7_seg_disp_encoder_1_b),
    .c(n7_seg_disp_encoder_1_c), .d(n7_seg_disp_encoder_1_d), .e(n7_seg_disp_encoder_1_e),
    .f(n7_seg_disp_encoder_1_f), .g(n7_seg_disp_encoder_1_g));
  _7_SEG_DISP_ENCODER u_7_seg_disp_encoder_2 (
    .in_1(_1_s_place), .a(n7_seg_disp_encoder_2_a), .b(n7_seg_disp_encoder_2_b), .c(n7_seg_disp_encoder_2_c),
    .d(n7_seg_disp_encoder_2_d), .e(n7_seg_disp_encoder_2_e), .f(n7_seg_disp_encoder_2_f),
    .g(n7_seg_disp_encoder_2_g));
  _7_Segment_Display u_7_segment_display_1 (
    .g(n7_seg_disp_encoder_1_g), .f(n7_seg_disp_encoder_1_f), .a(n7_seg_disp_encoder_1_a),
    .b(n7_seg_disp_encoder_1_b), .e(n7_seg_disp_encoder_1_e), .d(n7_seg_disp_encoder_1_d),
    .c(n7_seg_disp_encoder_1_c));  // open: dp
  _7_Segment_Display u_7_segment_display_2 (
    .g(n7_seg_disp_encoder_2_g), .f(n7_seg_disp_encoder_2_f), .a(n7_seg_disp_encoder_2_a),
    .b(n7_seg_disp_encoder_2_b), .e(n7_seg_disp_encoder_2_e), .d(n7_seg_disp_encoder_2_d),
    .c(n7_seg_disp_encoder_2_c));  // open: dp

  // Notes on the sheet:
  //   0-23 up counter
  //   with parallel loading
endmodule
