// Logisim project 001910501060_RahulManna_TrafficSignal.circ as structural Verilog: 9 circuits, main circuit main
module main (
  input  Make_busy,
  input  Reset,
  input  Pause,
  input  [3:0] H_10_s_place,
  input  [3:0] H_1_s_place,
  input  [3:0] M_10_s_place,
  input  [3:0] M_1_s_place,
  input  [3:0] S_10_s_place,
  input  [3:0] S_1_s_place
);

  wire and_1_out, and_2_out, and_3_out, and_4_out, Busy_hr_selector_busy, Clock_out, demultiplexer_1_out0,
       demultiplexer_1_out1, demultiplexer_1_out2, demultiplexer_1_out3, Load_out, multiplexer_1_out,
       not_1_out, not_2_out, not_3_out, not_4_out, not_5_out, not_6_out, not_7_out, not_8_out, not_9_out,
       not_10_out, not_11_out, not_12_out, not_13_out, or_1_out, or_2_out, Reset_out;
  wire [3:0] HH__1_s_place, HH__10_s_place, MM__1_s_place, MM__10_s_place, Mod_4_out, SS__1_s_place,
       SS__10_s_place, trafic_timer_30_60_1__1_s_place, trafic_timer_30_60_1__10_s_place;

  Button Load (.out(Load_out));
  Clock Clock (.out(Clock_out));
  Button u_Reset (.out(Reset_out));
  or or_1 (or_1_out, Clock_out, Pause);
  _0_23_counter HH (
    .Load(Load_out), .Clock(and_1_out), .Reset(Reset_out), .set_10_s_place(H_10_s_place),
    .set_1_s_place(H_1_s_place), ._10_s_place(HH__10_s_place), ._1_s_place(HH__1_s_place));
  Hex_Digit_Display hex_digit_display_1 (.value(HH__10_s_place));  // open: dp
  Hex_Digit_Display hex_digit_display_2 (.value(HH__1_s_place));  // open: dp
  and and_1 (and_1_out, not_1_out, MM__10_s_place[2], not_2_out, MM__10_s_place[0]);
  Busy_hr_selector Busy_hr_selector (._10_s(HH__10_s_place), ._1_s(HH__1_s_place), .Busy(Busy_hr_selector_busy));
  Hex_Digit_Display hex_digit_display_3 (.value(MM__10_s_place));  // open: dp
  _0_59_counter MM (
    .Load(Load_out), .Clock(and_2_out), .Reset(Reset_out), .set_10_s_place(M_10_s_place),
    .set_1_s_place(M_1_s_place), ._10_s_place(MM__10_s_place), ._1_s_place(MM__1_s_place));
  not not_1 (not_1_out, MM__10_s_place[3]);
  not not_2 (not_2_out, MM__10_s_place[1]);
  or or_2 (or_2_out, Make_busy, Busy_hr_selector_busy);
  Hex_Digit_Display hex_digit_display_4 (.value(MM__1_s_place));  // open: dp
  and and_2 (and_2_out, not_4_out, SS__10_s_place[2], not_5_out, SS__10_s_place[0]);
  not not_3 (not_3_out, or_2_out);
  Hex_Digit_Display hex_digit_display_5 (.value(SS__10_s_place));  // open: dp
  Hex_Digit_Display hex_digit_display_6 (.value(SS__1_s_place));  // open: dp
  _0_59_counter SS (
    .Load(Load_out), .Clock(or_1_out), .Reset(Reset_out), .set_10_s_place(S_10_s_place),
    .set_1_s_place(S_1_s_place), ._10_s_place(SS__10_s_place), ._1_s_place(SS__1_s_place));
  not not_4 (not_4_out, SS__10_s_place[3]);
  not not_5 (not_5_out, SS__10_s_place[1]);
  Demultiplexer #(.select(2), .enable("false")) demultiplexer_1 (
    .out0(demultiplexer_1_out0), .out1(demultiplexer_1_out1), .out2(demultiplexer_1_out2),
    .out3(demultiplexer_1_out3), .in(1'b1), .sel(Mod_4_out[1:0]));
  trafic_timer_30_60 trafic_timer_30_60_1 (
    .Not_busy(not_3_out), .Clock(Clock_out), .Reset(Reset), ._10_s_place(trafic_timer_30_60_1__10_s_place),
    ._1_s_place(trafic_timer_30_60_1__1_s_place));
  // Probe on H_10_s_place
  Hex_Digit_Display hex_digit_display_7 (.value(trafic_timer_30_60_1__10_s_place));  // open: dp
  and and_3 (and_3_out, not_6_out, not_7_out, trafic_timer_30_60_1__10_s_place[1], trafic_timer_30_60_1__10_s_place[0]);
  // Probe on H_1_s_place
  Hex_Digit_Display hex_digit_display_8 (.value(trafic_timer_30_60_1__1_s_place));  // open: dp
  not not_6 (not_6_out, trafic_timer_30_60_1__10_s_place[3]);
  not not_7 (not_7_out, trafic_timer_30_60_1__10_s_place[2]);
  not not_8 (not_8_out, trafic_timer_30_60_1__10_s_place[3]);
  and and_4 (and_4_out, not_8_out, trafic_timer_30_60_1__10_s_place[2], not_9_out, trafic_timer_30_60_1__10_s_place[0]);
  not not_9 (not_9_out, trafic_timer_30_60_1__10_s_place[1]);
  // Probe on M_10_s_place
  Hex_Digit_Display hex_digit_display_9 (.value(Mod_4_out));  // open: dp
  Multiplexer #(.disabled(0), .enable("false")) multiplexer_1 (
    .in0(and_4_out), .in1(and_3_out), .out(multiplexer_1_out), .sel(not_3_out));
  // Probe on M_1_s_place
  not not_10 (not_10_out, demultiplexer_1_out3);
  LED green (.in(demultiplexer_1_out3));
  LED red (.in(not_10_out));
  LED red_2 (.in(not_11_out));
  LED green_2 (.in(demultiplexer_1_out2));
  not not_11 (not_11_out, demultiplexer_1_out2);
  Mod4 Mod_4 (.clock(multiplexer_1_out), .Out(Mod_4_out));
  // Probe on S_10_s_place
  not not_12 (not_12_out, demultiplexer_1_out0);
  LED red_3 (.in(not_12_out));
  LED green_3 (.in(demultiplexer_1_out0));
  LED red_4 (.in(not_13_out));
  LED green_4 (.in(demultiplexer_1_out1));
  not not_13 (not_13_out, demultiplexer_1_out1);
  // Probe on S_1_s_place

  // Notes on the sheet:
  //   :
  //   :
endmodule

module MOD10_up_counter (
  input  Load,
  input  Clock,
  input  [3:0] Set_to,
  input  Reset,
  output [3:0] OUT
);

  wire and_1_out, and_2_out, and_3_out, and_4_out, and_5_out, and_6_out, and_7_out, and_8_out, and_9_out,
       and_10_out, and_11_out, FF3_qn, not_1_out, not_2_out, not_3_out, not_4_out, or_1_out, or_2_out,
       or_3_out, or_4_out;

  J_K_Flip_Flop #(.trigger("falling")) FF3 (
    .J(and_3_out), .clk(Clock), .K(OUT[0]), .Q(OUT[3]), .Qn(FF3_qn), .preset(and_4_out), .reset(or_1_out));  // open: en
  J_K_Flip_Flop #(.trigger("falling")) FF2 (
    .J(and_1_out), .clk(Clock), .K(and_1_out), .Q(OUT[2]), .preset(and_5_out), .reset(or_2_out));  // open: Qn, en
  J_K_Flip_Flop #(.trigger("falling")) FF0 (
    .J(and_2_out), .clk(Clock), .K(OUT[0]), .Q(OUT[1]), .preset(and_6_out), .reset(or_3_out));  // open: Qn, en
  J_K_Flip_Flop #(.trigger("falling")) FF0_2 (
    .J(1'b1), .clk(Clock), .K(1'b1), .Q(OUT[0]), .preset(and_7_out), .reset(or_4_out));  // open: Qn, en
  and and_1 (and_1_out, OUT[0], OUT[1]);
  and and_2 (and_2_out, OUT[0], FF3_qn);
  // Probe on OUT
  and and_3 (and_3_out, and_1_out, OUT[2]);
  or or_1 (or_1_out, Reset, and_8_out);
  and and_4 (and_4_out, Set_to[3], Load);
  or or_2 (or_2_out, Reset, and_9_out);
  and and_5 (and_5_out, Set_to[2], Load);
  or or_3 (or_3_out, Reset, and_10_out);
  and and_6 (and_6_out, Set_to[1], Load);
  or or_4 (or_4_out, Reset, and_11_out);
  and and_7 (and_7_out, Set_to[0], Load);
  and and_8 (and_8_out, Load, not_1_out);
  not not_1 (not_1_out, Set_to[3]);
  and and_9 (and_9_out, Load, not_2_out);
  not not_2 (not_2_out, Set_to[2]);
  and and_10 (and_10_out, Load, not_3_out);
  not not_3 (not_3_out, Set_to[1]);
  and and_11 (and_11_out, Load, not_4_out);
  not not_4 (not_4_out, Set_to[0]);
endmodule

module MOD_6_up_counter (
  input  Load,
  input  Clock,
  input  [3:0] Set_to,
  input  Reset,
  output [3:0] OUT
);

  wire and_1_out, and_2_out, and_3_out, and_4_out, and_5_out, and_6_out, and_7_out, and_8_out, FF2_qn,
       not_2_out, not_3_out, not_4_out, or_1_out, or_2_out, or_3_out;

  J_K_Flip_Flop #(.trigger("falling")) FF2 (
    .J(and_1_out), .clk(Clock), .K(OUT[0]), .Q(OUT[2]), .Qn(FF2_qn), .preset(and_3_out), .reset(or_1_out));  // open: en
  J_K_Flip_Flop #(.trigger("falling")) FF1 (
    .J(and_2_out), .clk(Clock), .K(OUT[0]), .Q(OUT[1]), .preset(and_4_out), .reset(or_2_out));  // open: Qn, en
  J_K_Flip_Flop #(.trigger("falling")) FF0 (
    .J(1'b1), .clk(Clock), .K(1'b1), .Q(OUT[0]), .preset(and_5_out), .reset(or_3_out));  // open: Qn, en
  and and_1 (and_1_out, OUT[0], OUT[1]);
  and and_2 (and_2_out, OUT[0], FF2_qn);
  not not_1 (OUT[3], 1'b1);
  // Probe on OUT
  or or_1 (or_1_out, Reset, and_6_out);
  and and_3 (and_3_out, Set_to[2], Load);
  or or_2 (or_2_out, Reset, and_7_out);
  and and_4 (and_4_out, Set_to[1], Load);
  or or_3 (or_3_out, Reset, and_8_out);
  and and_5 (and_5_out, Set_to[0], Load);
  and and_6 (and_6_out, Load, not_2_out);
  and and_7 (and_7_out, Load, not_3_out);
  and and_8 (and_8_out, Load, not_4_out);
  not not_2 (not_2_out, Set_to[2]);
  not not_3 (not_3_out, Set_to[1]);
  not not_4 (not_4_out, Set_to[0]);
endmodule

module _7_SEG_DISP_ENCODER (
  input  [3:0] in_1,
  output a,
  output b,
  output c,
  output d,
  output e,
  output f,
  output g
);

  wire and_1_out, and_2_out, and_3_out, and_4_out, and_5_out, and_6_out, and_7_out, and_8_out, and_9_out,
       and_10_out, and_11_out, and_12_out, and_13_out, and_14_out, and_15_out, and_16_out, and_17_out,
       not_1_out, not_2_out, not_3_out, not_4_out, not_5_out, not_6_out, not_7_out, not_8_out, not_9_out,
       not_10_out, not_11_out, not_12_out, not_13_out, not_14_out, not_15_out, not_16_out, not_17_out,
       not_18_out, not_19_out, not_20_out, not_21_out, or_1_out, or_2_out, or_3_out, or_4_out, or_6_out,
       or_8_out, or_9_out, or_10_out, or_11_out, or_14_out, or_15_out;

  not not_1 (not_1_out, in_1[2]);
  not not_2 (not_2_out, in_1[0]);
  not not_3 (not_3_out, in_1[1]);
  not not_4 (not_4_out, in_1[0]);
  not not_5 (not_5_out, in_1[1]);
  not not_6 (not_6_out, in_1[2]);
  not not_7 (not_7_out, in_1[0]);
  not not_8 (not_8_out, in_1[2]);
  not not_9 (not_9_out, in_1[1]);
  not not_10 (not_10_out, in_1[2]);
  not not_11 (not_11_out, in_1[0]);
  not not_12 (not_12_out, in_1[0]);
  not not_13 (not_13_out, in_1[1]);
  not not_14 (not_14_out, in_1[0]);
  not not_15 (not_15_out, in_1[1]);
  not not_16 (not_16_out, in_1[0]);
  not not_17 (not_17_out, in_1[2]);
  not not_18 (not_18_out, in_1[1]);
  not not_19 (not_19_out, in_1[0]);
  and and_1 (and_1_out, not_1_out, not_2_out);
  and and_2 (and_2_out, in_1[2], in_1[0]);
  not not_20 (not_20_out, in_1[2]);
  and and_3 (and_3_out, not_3_out, not_4_out);
  or or_1 (or_1_out, not_5_out, in_1[0]);
  and and_4 (and_4_out, not_6_out, not_7_out);
  and and_5 (and_5_out, not_8_out, in_1[1]);
  not not_21 (not_21_out, in_1[0]);
  and and_6 (and_6_out, in_1[2], not_9_out);
  and and_7 (and_7_out, not_10_out, not_11_out);
  and and_8 (and_8_out, in_1[1], not_12_out);
  and and_9 (and_9_out, not_13_out, not_14_out);
  and and_10 (and_10_out, in_1[2], not_15_out);
  and and_11 (and_11_out, in_1[2], not_16_out);
  and and_12 (and_12_out, not_17_out, in_1[1]);
  and and_13 (and_13_out, in_1[2], not_18_out);
  and and_14 (and_14_out, in_1[2], not_19_out);
  or or_2 (or_2_out, and_1_out, in_1[1]);
  or or_3 (or_3_out, and_2_out, in_1[3]);
  or or_4 (or_4_out, not_20_out, and_3_out);
  and and_15 (and_15_out, in_1[1], in_1[0]);
  or or_5 (c, or_1_out, in_1[2]);
  or or_6 (or_6_out, and_4_out, and_5_out);
  and and_16 (and_16_out, in_1[1], not_21_out);
  and and_17 (and_17_out, and_6_out, in_1[0]);
  or or_7 (e, and_7_out, and_8_out);
  or or_8 (or_8_out, and_9_out, and_10_out);
  or or_9 (or_9_out, and_11_out, in_1[3]);
  or or_10 (or_10_out, and_12_out, and_13_out);
  or or_11 (or_11_out, and_14_out, in_1[3]);
  or or_12 (a, or_2_out, or_3_out);
  or or_13 (b, or_4_out, and_15_out);
  or or_14 (or_14_out, or_6_out, and_16_out);
  or or_15 (or_15_out, and_17_out, in_1[3]);
  or or_16 (f, or_8_out, or_9_out);
  or or_17 (g, or_10_out, or_11_out);
  or or_18 (d, or_14_out, or_15_out);
  _7_Segment_Display u_7_segment_display_1 (.g(g), .f(f), .a(a), .b(b), .e(e), .d(d), .c(c));  // open: dp
endmodule

module _0_59_counter (
  input  Load,
  input  Clock,
  input  Reset,
  input  [3:0] set_10_s_place,
  input  [3:0] set_1_s_place,
  output [3:0] _10_s_place,
  output [3:0] _1_s_place
);

  wire and_1_out, n7_seg_disp_encoder_1_a, n7_seg_disp_encoder_1_b, n7_seg_disp_encoder_1_c,
       n7_seg_disp_encoder_1_d, n7_seg_disp_encoder_1_e, n7_seg_disp_encoder_1_f, n7_seg_disp_encoder_1_g,
       n7_seg_disp_encoder_2_a, n7_seg_disp_encoder_2_b, n7_seg_disp_encoder_2_c, n7_seg_disp_encoder_2_d,
       n7_seg_disp_encoder_2_e, n7_seg_disp_encoder_2_f, n7_seg_disp_encoder_2_g, not_1_out, not_2_out;

  and and_1 (and_1_out, _1_s_place[3], not_1_out, not_2_out, _1_s_place[0]);
  MOD_6_up_counter MOD_6 (.Load(Load), .Clock(and_1_out), .Set_to(set_10_s_place), .Reset(Reset), .OUT(_10_s_place));
  MOD10_up_counter MOD_10 (.Load(Load), .Clock(Clock), .Set_to(set_1_s_place), .Reset(Reset), .OUT(_1_s_place));
  not not_1 (not_1_out, _1_s_place[2]);
  not not_2 (not_2_out, _1_s_place[1]);
  _7_SEG_DISP_ENCODER u_7_seg_disp_encoder_1 (
    .in_1(_10_s_place), .a(n7_seg_disp_encoder_1_a), .b(n7_seg_disp_encoder_1_b),
    .c(n7_seg_disp_encoder_1_c), .d(n7_seg_disp_encoder_1_d), .e(n7_seg_disp_encoder_1_e),
    .f(n7_seg_disp_encoder_1_f), .g(n7_seg_disp_encoder_1_g));
  _7_SEG_DISP_ENCODER u_7_seg_disp_encoder_2 (
    .in_1(_1_s_place), .a(n7_seg_disp_encoder_2_a), .b(n7_seg_disp_encoder_2_b), .c(n7_seg_disp_encoder_2_c),
    .d(n7_seg_disp_encoder_2_d), .e(n7_seg_disp_encoder_2_e), .f(n7_seg_disp_encoder_2_f),
    .g(n7_seg_disp_encoder_2_g));
  _7_Segment_Display u_7_segment_display_1 (
    .g(n7_seg_disp_encoder_1_g), .f(n7_seg_disp_encoder_1_f), .a(n7_seg_disp_encoder_1_a),
    .b(n7_seg_disp_encoder_1_b), .e(n7_seg_disp_encoder_1_e), .d(n7_seg_disp_encoder_1_d),
    .c(n7_seg_disp_encoder_1_c));  // open: dp
  _7_Segment_Display u_7_segment_display_2 (
    .g(n7_seg_disp_encoder_2_g), .f(n7_seg_disp_encoder_2_f), .a(n7_seg_disp_encoder_2_a),
    .b(n7_seg_disp_encoder_2_b), .e(n7_seg_disp_encoder_2_e), .d(n7_seg_disp_encoder_2_d),
    .c(n7_seg_disp_encoder_2_c));  // open: dp
endmodule

module _0_23_counter (
  input  Load,
  input  Clock,
  input  Reset,
  input  [3:0] set_10_s_place,
  input  [3:0] set_1_s_place,
  output [3:0] _10_s_place,
  output [3:0] _1_s_place
);

  wire and_1_out, and_2_out, and_3_out, and_4_out, n7_seg_disp_encoder_1_a, n7_seg_disp_encoder_1_b,
       n7_seg_disp_encoder_1_c, n7_seg_disp_encoder_1_d, n7_seg_disp_encoder_1_e, n7_seg_disp_encoder_1_f,
       n7_seg_disp_encoder_1_g, n7_seg_disp_encoder_2_a, n7_seg_disp_encoder_2_b, n7_seg_disp_encoder_2_c,
       n7_seg_disp_encoder_2_d, n7_seg_disp_encoder_2_e, n7_seg_disp_encoder_2_f, n7_seg_disp_encoder_2_g,
       not_1_out, not_2_out, not_3_out, not_4_out, not_5_out, not_6_out, not_7_out, not_8_out, or_1_out;

  or or_1 (or_1_out, Reset, and_2_out);
  and and_1 (and_1_out, _1_s_place[3], not_1_out, not_2_out, _1_s_place[0]);
  and and_2 (and_2_out, and_3_out, and_4_out);
  MOD_6_up_counter MOD_6 (.Load(Load), .Clock(and_1_out), .Set_to(set_10_s_place), .Reset(or_1_out), .OUT(_10_s_place));
  MOD10_up_counter MOD_10 (.Load(Load), .Clock(Clock), .Set_to(set_1_s_place), .Reset(or_1_out), .OUT(_1_s_place));
  not not_1 (not_1_out, _1_s_place[2]);
  not not_2 (not_2_out, _1_s_place[1]);
  and and_3 (and_3_out, not_3_out, not_4_out, _10_s_place[1], not_5_out);
  not not_3 (not_3_out, _10_s_place[3]);
  not not_4 (not_4_out, _10_s_place[2]);
  not not_5 (not_5_out, _10_s_place[0]);
  and and_4 (and_4_out, not_6_out, _1_s_place[2], not_7_out, not_8_out);
  not not_6 (not_6_out, _1_s_place[3]);
  not not_7 (not_7_out, _1_s_place[1]);
  not not_8 (not_8_out, _1_s_place[0]);
  _7_SEG_DISP_ENCODER u_7_seg_disp_encoder_1 (
    .in_1(_10_s_place), .a(n7_seg_disp_encoder_1_a), .b(n7_seg_disp_encoder_1_b),
    .c(n7_seg_disp_encoder_1_c), .d(n7_seg_disp_encoder_1_d), .e(n7_seg_disp_encoder_1_e),
    .f(n7_seg_disp_encoder_1_f), .g(n7_seg_disp_encoder_1_g));
  _7_SEG_DISP_ENCODER u_7_seg_disp_encoder_2 (
    .in_1(_1_s_place), .a(n7_seg_disp_encoder_2_a), .b(n7_seg_disp_encoder_2_b), .c(n7_seg_disp_encoder_2_c),
    .d(n7_seg_disp_encoder_2_d), .e(n7_seg_disp_encoder_2_e), .f(n7_seg_disp_encoder_2_f),
    .g(n7_seg_disp_encoder_2_g));
  _7_Segment_Display u_7_segment_display_1 (
    .g(n7_seg_disp_encoder_1_g), .f(n7_seg_disp_encoder_1_f), .a(n7_seg_disp_encoder_1_a),
    .b(n7_seg_disp_encoder_1_b), .e(n7_seg_disp_encoder_1_e), .d(n7_seg_disp_encoder_1_d),
    .c(n7_seg_disp_encoder_1_c));  // open: dp
  _7_Segment_Display u_7_segment_display_2 (
    .g(n7_seg_disp_encoder_2_g), .f(n7_seg_disp_encoder_2_f), .a(n7_seg_disp_encoder_2_a),
    .b(n7_seg_disp_encoder_2_b), .e(n7_seg_disp_encoder_2_e), .d(n7_seg_disp_encoder_2_d),
    .c(n7_seg_disp_encoder_2_c));  // open: dp
endmodule

module trafic_timer_30_60 (
  input  Not_busy,
  input  Clock,
  input  Reset,
  output [3:0] _10_s_place,
  output [3:0] _1_s_place
);

  wire and_1_out, and_2_out, and_3_out, n7_seg_disp_encoder_1_a, n7_seg_disp_encoder_1_b,
       n7_seg_disp_encoder_1_c, n7_seg_disp_encoder_1_d, n7_seg_disp_encoder_1_e, n7_seg_disp_encoder_1_f,
       n7_seg_disp_encoder_1_g, n7_seg_disp_encoder_2_a, n7_seg_disp_encoder_2_b, n7_seg_disp_encoder_2_c,
       n7_seg_disp_encoder_2_d, n7_seg_disp_encoder_2_e, n7_seg_disp_encoder_2_f, n7_seg_disp_encoder_2_g,
       not_1_out, not_2_out, not_3_out, not_4_out, or_1_out;

  or or_1 (or_1_out, Reset, and_1_out);
  and and_1 (and_1_out, and_3_out, Not_busy);
  and and_2 (and_2_out, _1_s_place[3], not_1_out, not_2_out, _1_s_place[0]);
  MOD_6_up_counter MOD_6 (.Clock(and_2_out), .Reset(or_1_out), .OUT(_10_s_place));  // open: Load, Set_to
  MOD10_up_counter MOD_10 (.Clock(Clock), .Reset(Reset), .OUT(_1_s_place));  // open: Load, Set_to
  not not_1 (not_1_out, _1_s_place[2]);
  not not_2 (not_2_out, _1_s_place[1]);
  and and_3 (and_3_out, not_3_out, not_4_out, _10_s_place[1], _10_s_place[0]);
  not not_3 (not_3_out, _10_s_place[3]);
  not not_4 (not_4_out, _10_s_place[2]);
  _7_SEG_DISP_ENCODER u_7_seg_disp_encoder_1 (
    .in_1(_10_s_place), .a(n7_seg_disp_encoder_1_a), .b(n7_seg_disp_encoder_1_b),
    .c(n7_seg_disp_encoder_1_c), .d(n7_seg_disp_encoder_1_d), .e(n7_seg_disp_encoder_1_e),
    .f(n7_seg_disp_encoder_1_f), .g(n7_seg_disp_encoder_1_g));
  _7_SEG_DISP_ENCODER u_7_seg_disp_encoder_2 (
    .in_1(_1_s_place), .a(n7_seg_disp_encoder_2_a), .b(n7_seg_disp_encoder_2_b), .c(n7_seg_disp_encoder_2_c),
    .d(n7_seg_disp_encoder_2_d), .e(n7_seg_disp_encoder_2_e), .f(n7_seg_disp_encoder_2_f),
    .g(n7_seg_disp_encoder_2_g));
  _7_Segment_Display u_7_segment_display_1 (
    .g(n7_seg_disp_encoder_1_g), .f(n7_seg_disp_encoder_1_f), .a(n7_seg_disp_encoder_1_a),
    .b(n7_seg_disp_encoder_1_b), .e(n7_seg_disp_encoder_1_e), .d(n7_seg_disp_encoder_1_d),
    .c(n7_seg_disp_encoder_1_c));  // open: dp
  _7_Segment_Display u_7_segment_display_2 (
    .g(n7_seg_disp_encoder_2_g), .f(n7_seg_disp_encoder_2_f), .a(n7_seg_disp_encoder_2_a),
    .b(n7_seg_disp_encoder_2_b), .e(n7_seg_disp_encoder_2_e), .d(n7_seg_disp_encoder_2_d),
    .c(n7_seg_disp_encoder_2_c));  // open: dp

  // Notes on the sheet:
  //   Timer for traffic control
  //   (0-30 when not busy and 0-60 when busy)
endmodule

module Mod4 (
  input  clock,
  output [3:0] Out
);

  T_Flip_Flop #(.trigger("falling")) t_ff_1 (.clk(clock), .T(Out[0]), .Q(Out[1]));  // open: Qn, preset, reset, en
  T_Flip_Flop #(.trigger("falling")) t_ff_2 (.clk(clock), .T(1'b1), .Q(Out[0]));  // open: Qn, preset, reset, en
  not not_1 (Out[3], 1'b1);
  Hex_Digit_Display hex_digit_display_1 (.value({{2{Out[3]}}, Out[1:0]}));  // open: dp

  assign Out[2] = Out[3];

  // Notes on the sheet:
  //   Mod 4 counter
endmodule

module Busy_hr_selector (
  input  [3:0] _10_s,
  input  [3:0] _1_s,
  output Busy
);

  wire and_1_out, and_2_out, and_3_out, and_4_out, and_5_out, and_6_out, and_7_out, and_8_out, and_9_out,
       not_1_out, not_2_out, not_3_out, not_4_out, not_5_out, not_6_out, not_7_out, not_8_out, not_9_out,
       not_10_out, not_11_out, not_12_out, not_13_out;

  not not_1 (not_1_out, _10_s[3]);
  not not_2 (not_2_out, _10_s[2]);
  not not_3 (not_3_out, _10_s[1]);
  not not_4 (not_4_out, _10_s[0]);
  not not_5 (not_5_out, _1_s[2]);
  not not_6 (not_6_out, _1_s[1]);
  and and_1 (and_1_out, not_1_out, not_2_out, not_3_out, not_4_out);
  and and_2 (and_2_out, _1_s[3], not_5_out, not_6_out, _1_s[0]);
  not not_7 (not_7_out, _10_s[3]);
  not not_8 (not_8_out, _10_s[2]);
  not not_9 (not_9_out, _10_s[1]);
  not not_10 (not_10_out, _1_s[2]);
  not not_11 (not_11_out, _1_s[1]);
  not not_12 (not_12_out, _1_s[0]);
  and and_3 (and_3_out, not_7_out, not_8_out, not_9_out, _10_s[0]);
  and and_4 (and_4_out, _1_s[3], not_10_out, not_11_out, not_12_out);
  not not_13 (not_13_out, _1_s[3]);
  and and_5 (and_5_out, not_13_out, _1_s[2], _1_s[1], _1_s[0]);
  and and_6 (and_6_out, and_1_out, and_4_out);
  and and_7 (and_7_out, and_3_out, and_5_out);
  and and_8 (and_8_out, and_1_out, and_2_out);
  and and_9 (and_9_out, and_3_out, and_4_out);
  or or_1 (Busy, and_9_out, and_7_out, and_8_out, and_6_out);

  // Notes on the sheet:
  //   Busy hour selector
  //   Busy hours : 08:00:00 - 09:59:59 and 17:00:00 - 18:59:59
endmodule
